# Fritzing sketch Schematic_pico-2fa-token (saved by Fritzing 0.9.5d)
breadboards: 1

parts:
  Mod1 = Raspberry Pi Pico
  S1 = Pushbutton [package="[THT]"]
  S2 = Pushbutton [package="[THT]"]
  S3 = Pushbutton [package="[THT]"]
  LCD1 = LCD screen
  LCM1602_IIC1 = LCM1602 IIC [part_number="LCM1602 IIC" chip_label="LCM1602 IIC" package="DIP (Dual Inline) [THT]"]

nets:
  N1: Mod1.pin_3, Mod1.pin_8, Mod1.pin_13, Mod1.pin_18, Mod1.pin_23, Mod1.pin_28, Mod1.pin_33, Mod1.pin_38, S1.Pin_1, S1.Pin_2, S2.Pin_1, S2.Pin_2, S3.Pin_1, S3.Pin_2, LCM1602_IIC1.GND
  N2: Mod1.pin_6, LCM1602_IIC1.SDA
  N3: Mod1.pin_7, LCM1602_IIC1.VCC
  N4: Mod1.pin_17, S1.Pin_3, S1.Pin_4
  N5: Mod1.pin_19, S2.Pin_3, S2.Pin_4
  N6: Mod1.pin_20, S3.Pin_3, S3.Pin_4
  N7: Mod1.pin_36, LCM1602_IIC1.SCL
  N8: Mod1.pin_40, LCD1.VDD, LCD1.LED+
  VSS: LCD1.VSS, LCM1602_IIC1.VSS
  N9: LCD1.RS, LCM1602_IIC1.RS
  N10: LCD1.R/W, LCM1602_IIC1.RW
  N11: LCD1.E, LCM1602_IIC1.E
  N12: LCD1.DB4, LCM1602_IIC1.D4
  N13: LCD1.DB5, LCM1602_IIC1.D5
  N14: LCD1.DB6, LCM1602_IIC1.D6
  N15: LCD1.DB7, LCM1602_IIC1.D7
  N16: LCD1.LED-, LCM1602_IIC1.K
  N17: LCM1602_IIC1.LED_A, LCM1602_IIC1.LED_B

custom parts:
  Raspberry Pi Pico: Raspberry Pi Pico. Based around the RP2040 microcontroller the Pico is a low cost microcontroller device bringing Raspberry Pi quality, cost, and easy of use to the microcontroller space. Jan 2021, Split part in to two versions: tht (this one) and SMD. This one will drill holes for a .1 in header in pcb to allow plugging in the module as well as providing pads to solder the module to the top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
  LCM1602 IIC: I2C-Module to use a 1602 or 2004 LCD on with the wire.h libory Serial LCD Modul
